// Logisim project regfile.circ as structural Verilog: 1 circuit, main circuit RegFile
module RegFile (
  input  [4:0] RD,
  input  [4:0] RS1,
  input  [4:0] RS2,
  input  [31:0] W,
  input  WE,
  input  Clk,
  output [31:0] s0,
  output [31:0] s1,
  output [31:0] t0,
  output [31:0] t1,
  output [31:0] a0,
  output [31:0] ra,
  output [31:0] sp,
  output [31:0] R1,
  output [31:0] R2
);

  wire and_2_out, and_3_out, and_4_out, and_5_out, and_6_out, and_7_out, Clk_t, decoder_1_out0,
       decoder_1_out1, decoder_1_out3, decoder_1_out5, decoder_1_out7, decoder_1_out9, decoder_1_out11,
       decoder_1_out17;
  wire [31:0] a1_q, Zero_q;
  wire [31:1] GROUND;

  Decoder #(.select(5)) decoder_1 (
    .out0(decoder_1_out0), .out1(decoder_1_out1), .out3(decoder_1_out3), .out5(decoder_1_out5),
    .out7(decoder_1_out7), .out9(decoder_1_out9), .out11(decoder_1_out11), .out17(decoder_1_out17), .sel(RD));  // open: out2, out4, out6, out8, out10, out12, out13, out14, out15, out16, out18, out19, out20, out21, out22, out23, out24, out25, out26, out27, out28, out29, out30, out31, en
  // AND_Gate and_1 has open pins: in0=WE, in4=decoder_1_out1, out=open
  and and_2 (and_2_out, WE, decoder_1_out17);
  and and_3 (and_3_out, WE, decoder_1_out3);
  and and_4 (and_4_out, WE, decoder_1_out5);
  and and_5 (and_5_out, WE, decoder_1_out7);
  and and_6 (and_6_out, WE, decoder_1_out9);
  and and_7 (and_7_out, WE, decoder_1_out11);
  Register #(.width(32)) Zero (.D({GROUND, 1'b0}), .en(decoder_1_out0), .Q(Zero_q), .clk(Clk_t));  // open: clr
  Register #(.width(32)) u_ra (.D(W), .en(and_2_out), .Q(ra), .clk(Clk_t));  // open: clr
  Register #(.width(32)) u_sp (.D(W), .Q(sp), .clk(Clk_t));  // open: en, clr
  Register #(.width(32)) u_t0 (.D(W), .en(and_3_out), .Q(t0), .clk(Clk_t));  // open: clr
  Register #(.width(32)) u_t1 (.D(W), .en(and_4_out), .Q(t1), .clk(Clk_t));  // open: clr
  Register #(.width(32)) u_s0 (.D(W), .en(and_5_out), .Q(s0), .clk(Clk_t));  // open: clr
  Register #(.width(32)) u_s1 (.D(W), .Q(s1), .clk(Clk_t));  // open: en, clr
  Register #(.width(32)) u_a0 (.D(W), .en(and_6_out), .Q(a0), .clk(Clk_t));  // open: clr
  Register #(.width(32)) a1 (.D(W), .en(and_7_out), .Q(a1_q), .clk(Clk_t));  // open: clr
  Multiplexer #(.select(5), .width(32)) multiplexer_1 (
    .in0(Zero_q), .in1(ra), .in5(sp), .in11(t0), .in17(t1), .in23(s0), .in26(s1), .in29(a0), .in30(a1_q),
    .out(R1), .sel(RS1));  // open: in2, in3, in4, in6, in7, in8, in9, in10, in12, in13, in14, in15, in16, in18, in19, in20, in21, in22, in24, in25, in27, in28, in31, en
  Multiplexer #(.select(5), .width(32)) multiplexer_2 (
    .in0(Zero_q), .in10(ra), .in11(sp), .in12(t0), .in13(t1), .in14(s0), .in15(s1), .in17(a0), .in18(a1_q),
    .out(R2), .sel(RS2));  // open: in1, in2, in3, in4, in5, in6, in7, in8, in9, in16, in19, in20, in21, in22, in23, in24, in25, in26, in27, in28, in29, in30, in31, en
  // Pins of 1 and 32 bits meet at {GROUND, 1'b0}

  // Notes on the sheet:
  //   Write Register
  //   Read Register 1
  //   Read Register 2
  //   Write Data
  //   Write Enable
  //   Clock
  //   NOTE
  //   Please do not modify/replace/move/change/delete/etc input and output pins
  //   These are debug/test outputs from your circuit
  //   Read Data 1
  //   Read Data 2
endmodule
